// Logisim project Aula_1.circ as structural Verilog: 7 circuits, main circuit main
module main (
  input  [3:0] A,
  input  [3:0] B,
  output [3:0] S
);

  Somador_Completo somador_completo_1 (.S(S[3]), .Cout(S[3]));  // open: B, Cin, A
  Somador_Completo somador_completo_2 (.S(S[2]), .B(S[2]), .Cin(S[1]), .Cout(S[1]));  // open: A
  Hex_Digit_Display hex_digit_display_1 (.value(S));  // open: dp
  Somador_Completo somador_completo_3 (.S(S[1]), .Cout(S[1]));  // open: B, Cin, A
  Somador_Completo somador_completo_4 (.S(S[0]), .Cout(S[0]));  // open: B, Cin, A
endmodule

module Meio_Somador (
  input  in_1,
  input  in_2,
  output S,
  output Cout
);

  xor xor_1 (S, in_1, in_2);
  and and_1 (Cout, in_1, in_2);
endmodule

module Somador_Completo (
  input  A,
  input  B,
  input  Cin,
  output S,
  output Cout
);

  wire meio_somador_1_cout, meio_somador_1_s, meio_somador_2_cout;

  Meio_Somador meio_somador_1 (.Cout(meio_somador_1_cout), .in_2(B), .in_1(A), .S(meio_somador_1_s));
  Meio_Somador meio_somador_2 (.Cout(meio_somador_2_cout), .in_2(Cin), .in_1(meio_somador_1_s), .S(S));
  or or_1 (Cout, meio_somador_2_cout, meio_somador_1_cout);
endmodule

module Meio_subtrator (
  input  A,
  input  B,
  output S,
  output Tout
);

  wire not_1_out;

  not not_1 (not_1_out, A);
  xor xor_1 (S, A, B);
  and and_1 (Tout, B, not_1_out);
endmodule

module Subtrator_Completo (
  input  A,
  input  B,
  input  Tin,
  output S,
  output Tout
);

  wire meio_subtrator_1_s, meio_subtrator_1_tout, meio_subtrator_2_tout;

  Meio_subtrator meio_subtrator_1 (.Tout(meio_subtrator_1_tout), .S(meio_subtrator_1_s), .B(B), .A(A));
  Meio_subtrator meio_subtrator_2 (.Tout(meio_subtrator_2_tout), .S(S), .B(Tin), .A(meio_subtrator_1_s));
  or or_1 (Tout, meio_subtrator_2_tout, meio_subtrator_1_tout);
endmodule

module Exercicio_1 (
  input  A,
  input  K2,
  input  K1,
  input  B,
  output S,
  output Cout_Tout
);

  wire [1:0] demultiplexer_1_out0, demultiplexer_1_out1, meio_somador_1_s, meio_subtrator_1_s;

  Demultiplexer #(.width(2), .enable("false")) demultiplexer_1 (
    .out0(demultiplexer_1_out0), .out1(demultiplexer_1_out1), .in({B, A}), .sel(K1));
  Meio_Somador meio_somador_1 (
    .Cout(meio_somador_1_s[1]), .in_2(demultiplexer_1_out0[1]), .in_1(demultiplexer_1_out0[0]),
    .S(meio_somador_1_s[0]));
  Meio_subtrator meio_subtrator_1 (
    .Tout(meio_subtrator_1_s[1]), .S(meio_subtrator_1_s[0]), .B(demultiplexer_1_out1[1]),
    .A(demultiplexer_1_out1[0]));
  Multiplexer #(.width(2), .enable("false")) multiplexer_1 (
    .in0(meio_somador_1_s), .in1(meio_subtrator_1_s), .out({Cout_Tout, S}), .sel(K2));
endmodule

module Exercicio_2 (
  input  A,
  input  B,
  input  Cin,
  input  K1,
  input  K2,
  output S,
  output Cout_Tout
);

  wire [1:0] somador_completo_1_s, subtrator_completo_1_s;
  wire [2:0] demultiplexer_1_out0, demultiplexer_1_out1;

  Demultiplexer #(.width(3), .enable("false")) demultiplexer_1 (
    .out0(demultiplexer_1_out0), .out1(demultiplexer_1_out1), .in({Cin, B, A}), .sel(K1));
  Somador_Completo somador_completo_1 (
    .S(somador_completo_1_s[0]), .B(demultiplexer_1_out0[1]), .Cin(demultiplexer_1_out0[2]),
    .Cout(somador_completo_1_s[1]), .A(demultiplexer_1_out0[0]));
  Subtrator_Completo subtrator_completo_1 (
    .Tout(subtrator_completo_1_s[1]), .S(subtrator_completo_1_s[0]), .Tin(demultiplexer_1_out1[2]),
    .B(demultiplexer_1_out1[1]), .A(demultiplexer_1_out1[0]));
  Multiplexer #(.width(2), .enable("false")) multiplexer_1 (
    .in0(somador_completo_1_s), .in1(subtrator_completo_1_s), .out({Cout_Tout, S}), .sel(K2));
endmodule
