// Logisim project Aula_2.circ as structural Verilog
module Meio_Somador (
  input  in_1,
  input  in_2,
  output S,
  output Cout
);

  xor xor_1 (S, in_1, in_2);
  and and_1 (Cout, in_1, in_2);
endmodule

module Somador_Completo (
  input  A,
  input  B,
  input  Cin,
  output S,
  output Cout
);

  wire meio_somador_1_cout, meio_somador_1_s, meio_somador_2_cout;

  Meio_Somador meio_somador_1 (.S(meio_somador_1_s), .in_2(B), .in_1(A), .Cout(meio_somador_1_cout));
  Meio_Somador meio_somador_2 (.S(S), .in_2(Cin), .in_1(meio_somador_1_s), .Cout(meio_somador_2_cout));
  or or_1 (Cout, meio_somador_2_cout, meio_somador_1_cout);
endmodule

module Meio_subtrator (
  input  A,
  input  B,
  output S,
  output Tout
);

  wire not_1_out;

  not not_1 (not_1_out, A);
  xor xor_1 (S, A, B);
  and and_1 (Tout, B, not_1_out);
endmodule

module Subtrator_Completo (
  input  A,
  input  B,
  input  Tin,
  output S,
  output Tout
);

  wire meio_subtrator_1_s, meio_subtrator_1_tout, meio_subtrator_2_tout;

  Meio_subtrator meio_subtrator_1 (.A(A), .Tout(meio_subtrator_1_tout), .B(B), .S(meio_subtrator_1_s));
  Meio_subtrator meio_subtrator_2 (.A(meio_subtrator_1_s), .Tout(meio_subtrator_2_tout), .B(Tin), .S(S));
  or or_1 (Tout, meio_subtrator_2_tout, meio_subtrator_1_tout);
endmodule

module Exercicio_1 (
  input  A,
  input  K2,
  input  K1,
  input  B,
  output S,
  output Cout_Tout
);

  wire [1:0] demultiplexer_1_out0, demultiplexer_1_out1, meio_somador_1_s, meio_subtrator_1_s;

  Demultiplexer #(.width(2), .enable("false")) demultiplexer_1 (
    .out0(demultiplexer_1_out0), .out1(demultiplexer_1_out1), .in({B, A}), .sel(K1));
  Meio_Somador meio_somador_1 (
    .S(meio_somador_1_s[0]), .in_2(demultiplexer_1_out0[1]), .in_1(demultiplexer_1_out0[0]),
    .Cout(meio_somador_1_s[1]));
  Meio_subtrator meio_subtrator_1 (
    .A(demultiplexer_1_out1[0]), .Tout(meio_subtrator_1_s[1]), .B(demultiplexer_1_out1[1]),
    .S(meio_subtrator_1_s[0]));
  Multiplexer #(.width(2), .enable("false")) multiplexer_1 (
    .in0(meio_somador_1_s), .in1(meio_subtrator_1_s), .out({Cout_Tout, S}), .sel(K2));
endmodule

module Exercicio_2 (
  input  A,
  input  B,
  input  Cin,
  input  K1,
  input  K2,
  output S,
  output Cout_Tout
);

  wire [1:0] somador_completo_1_s, subtrator_completo_1_s;
  wire [2:0] demultiplexer_1_out0, demultiplexer_1_out1;

  Demultiplexer #(.width(3), .enable("false")) demultiplexer_1 (
    .out0(demultiplexer_1_out0), .out1(demultiplexer_1_out1), .in({Cin, B, A}), .sel(K1));
  Somador_Completo somador_completo_1 (
    .Cout(somador_completo_1_s[1]), .S(somador_completo_1_s[0]), .Cin(demultiplexer_1_out0[2]),
    .B(demultiplexer_1_out0[1]), .A(demultiplexer_1_out0[0]));
  Subtrator_Completo subtrator_completo_1 (
    .B(demultiplexer_1_out1[1]), .Tout(subtrator_completo_1_s[1]), .Tin(demultiplexer_1_out1[2]),
    .S(subtrator_completo_1_s[0]), .A(demultiplexer_1_out1[0]));
  Multiplexer #(.width(2), .enable("false")) multiplexer_1 (
    .in0(somador_completo_1_s), .in1(subtrator_completo_1_s), .out({Cout_Tout, S}), .sel(K2));
endmodule

module soma_sub_comp_2 (
  input  [3:0] A,
  input  [3:0] B,
  input  Cin,
  output Cout,
  output [3:0] S
);

  wire multiplexer_1_out, multiplexer_2_out, multiplexer_3_out, multiplexer_4_out, not_1_out, not_2_out,
       not_3_out, not_4_out, somador_completo_2_cout, somador_completo_3_cout, somador_completo_4_cout;

  Hex_Digit_Display hex_digit_display_1 (.value(S));  // open: dp
  not not_1 (not_1_out, B[3]);
  Multiplexer #(.enable("false")) multiplexer_1 (.in0(B[3]), .in1(not_1_out), .out(multiplexer_1_out), .sel(Cin));
  Somador_Completo somador_completo_1 (
    .Cout(Cout), .S(S[3]), .Cin(somador_completo_2_cout), .B(multiplexer_1_out), .A(A[3]));
  not not_2 (not_2_out, B[2]);
  Multiplexer #(.enable("false")) multiplexer_2 (.in0(B[2]), .in1(not_2_out), .out(multiplexer_2_out), .sel(Cin));
  Somador_Completo somador_completo_2 (
    .Cout(somador_completo_2_cout), .S(S[2]), .Cin(somador_completo_3_cout), .B(multiplexer_2_out), .A(A[2]));
  not not_3 (not_3_out, B[1]);
  Multiplexer #(.enable("false")) multiplexer_3 (.in0(B[1]), .in1(not_3_out), .out(multiplexer_3_out), .sel(Cin));
  Somador_Completo somador_completo_3 (
    .Cout(somador_completo_3_cout), .S(S[1]), .Cin(somador_completo_4_cout), .B(multiplexer_3_out), .A(A[1]));
  Multiplexer #(.enable("false")) multiplexer_4 (.in0(B[0]), .in1(not_4_out), .out(multiplexer_4_out), .sel(Cin));
  not not_4 (not_4_out, B[0]);
  Somador_Completo somador_completo_4 (
    .Cout(somador_completo_4_cout), .S(S[0]), .Cin(Cin), .B(multiplexer_4_out), .A(A[0]));
endmodule

module Multiplicador (
  input  A1,
  input  A0,
  input  B1,
  input  B0,
  output P3,
  output P2,
  output P1,
  output P0
);

  wire and_1_out, and_2_out, and_3_out, meio_somador_2_cout;

  and and_1 (and_1_out, A1, B1);
  and and_2 (and_2_out, A1, B0);
  Meio_Somador meio_somador_1 (.S(P2), .in_2(and_1_out), .in_1(meio_somador_2_cout), .Cout(P3));
  and and_3 (and_3_out, A0, B1);
  and and_4 (P0, A0, B0);
  Meio_Somador meio_somador_2 (.S(P1), .in_2(and_2_out), .in_1(and_3_out), .Cout(meio_somador_2_cout));

  // Notes on the sheet:
  //   Multiplicador
endmodule

module Registrador (
  input  [3:0] D,
  input  Clock,
  input  Carga,
  input  Clear,
  output [3:0] Q
);

  wire multiplexer_1_out, multiplexer_2_out, multiplexer_3_out, multiplexer_4_out;

  D_Flip_Flop d_ff_1 (.D(multiplexer_1_out), .clk(Clock), .Q(Q[0]), .reset(Clear));  // open: Qn, preset
  Multiplexer #(.enable("false")) multiplexer_1 (.in0(Q[0]), .in1(D[0]), .out(multiplexer_1_out), .sel(Carga));
  Multiplexer #(.enable("false")) multiplexer_2 (.in0(Q[1]), .in1(D[1]), .out(multiplexer_2_out), .sel(Carga));
  D_Flip_Flop d_ff_2 (.D(multiplexer_2_out), .clk(Clock), .Q(Q[1]), .reset(Clear));  // open: Qn, preset
  Multiplexer #(.enable("false")) multiplexer_3 (.in0(Q[2]), .in1(D[2]), .out(multiplexer_3_out), .sel(Carga));
  D_Flip_Flop d_ff_3 (.D(multiplexer_3_out), .clk(Clock), .Q(Q[2]), .reset(Clear));  // open: Qn, preset
  Multiplexer #(.enable("false")) multiplexer_4 (.in0(Q[3]), .in1(D[3]), .out(multiplexer_4_out), .sel(Carga));
  D_Flip_Flop d_ff_4 (.D(multiplexer_4_out), .clk(Clock), .Q(Q[3]), .reset(Clear));  // open: Qn, preset

  // Notes on the sheet:
  //   Registrador com Carga Paralela
endmodule
