// Logisim project Projeto.circ as structural Verilog: 6 circuits, main circuit main
module main (
  input  [3:0] A,
  input  [3:0] B,
  output [3:0] S
);

  Somador_Completo somador_completo_1 (.Cout(S[3]), .S(S[3]));  // open: B, Cin, A
  Somador_Completo somador_completo_2 (.B(S[2]), .Cout(S[1]), .Cin(S[1]), .S(S[2]));  // open: A
  Hex_Digit_Display hex_digit_display_1 (.value(S));  // open: dp
  Somador_Completo somador_completo_3 (.Cout(S[1]), .S(S[1]));  // open: B, Cin, A
  Somador_Completo somador_completo_4 (.Cout(S[0]), .S(S[0]));  // open: B, Cin, A
endmodule

module Meio_Somador (
  input  in_1,
  input  in_2,
  output S,
  output Cout
);

  xor xor_1 (S, in_1, in_2);
  and and_1 (Cout, in_1, in_2);
endmodule

module Somador_Completo (
  input  A,
  input  B,
  input  Cin,
  output S,
  output Cout
);

  wire meio_somador_1_cout, meio_somador_1_s, meio_somador_2_cout;

  Meio_Somador meio_somador_1 (.Cout(meio_somador_1_cout), .S(meio_somador_1_s), .in_1(A), .in_2(B));
  Meio_Somador meio_somador_2 (.Cout(meio_somador_2_cout), .S(S), .in_1(meio_somador_1_s), .in_2(Cin));
  or or_1 (Cout, meio_somador_2_cout, meio_somador_1_cout);
endmodule

module Meio_subtrator (
  input  A,
  input  B,
  output S,
  output Tout
);

  wire not_1_out;

  not not_1 (not_1_out, A);
  xor xor_1 (S, A, B);
  and and_1 (Tout, B, not_1_out);
endmodule

module Projeto (
  input  [7:0] A,
  input  [7:0] B,
  input  [2:0] SA,
  input  Cin,
  input  [3:0] OPCODE,
  output [7:0] S_16,
  output [7:0] S_10,
  output Cout
);

  wire [7:0] and_1_out, nor_1_out, or_1_out, shifter_1_out, shifter_2_out, somador_8_1_s, xor_1_out;

  Shifter shifter_1 (.in(B), .\dist (SA), .out(shifter_1_out));
  Shifter #(.shift("lr")) shifter_2 (.in(B), .\dist (SA), .out(shifter_2_out));
  assign and_1_out = B & A;  // AND_Gate and_1, 8 bits wide
  assign or_1_out = B | A;  // OR_Gate or_1, 8 bits wide
  assign xor_1_out = B ^ A;  // XOR_Gate xor_1, 8 bits wide
  assign nor_1_out = ~(B | A);  // NOR_Gate nor_1, 8 bits wide
  Somador_8 somador_8_1 (.Cout(Cout), .Cin(Cin), .A(A), .S(somador_8_1_s), .B(B));
  Multiplexer #(.select(4), .width(8), .enable("false")) multiplexer_1 (
    .in0(shifter_1_out), .in1({8{1'b0}}), .in2(nor_1_out), .in3({8{1'b0}}), .in4(xor_1_out),
    .in5(shifter_2_out), .in6({8{1'b0}}), .in7(somador_8_1_s), .in8({8{1'b0}}), .in9(and_1_out),
    .in10(somador_8_1_s), .in11({8{1'b0}}), .in12({8{1'b0}}), .in13({8{1'b0}}), .in14({8{1'b0}}),
    .in15(or_1_out), .out(S_10), .sel(OPCODE));
  Hex_Digit_Display hex_digit_display_1 (.value(OPCODE));  // open: dp

  assign S_16 = S_10;

  // Notes on the sheet:
  //   Porta AND
  //   Porta OR
  //   Porta XOR
  //   Porta NOR
  //   Shift Register - Left
  //   Shift Register - Right
  //   Somador/Subtrator Completo
endmodule

module Somador_8 (
  input  [7:0] B,
  input  Cin,
  input  [7:0] A,
  output Cout,
  output [7:0] S
);

  wire multiplexer_1_out, multiplexer_2_out, multiplexer_3_out, multiplexer_4_out, multiplexer_5_out,
       multiplexer_6_out, multiplexer_7_out, multiplexer_8_out, not_1_out, not_2_out, not_3_out, not_4_out,
       not_5_out, not_6_out, not_7_out, not_8_out, somador_completo_2_cout, somador_completo_3_cout,
       somador_completo_4_cout, somador_completo_5_cout, somador_completo_6_cout, somador_completo_7_cout,
       somador_completo_8_cout;

  not not_1 (not_1_out, B[7]);
  Multiplexer #(.enable("false")) multiplexer_1 (.in0(B[7]), .in1(not_1_out), .out(multiplexer_1_out), .sel(Cin));
  Somador_Completo somador_completo_1 (
    .B(multiplexer_1_out), .Cout(Cout), .Cin(somador_completo_2_cout), .S(S[7]), .A(A[7]));
  not not_2 (not_2_out, B[6]);
  Multiplexer #(.enable("false")) multiplexer_2 (.in0(B[6]), .in1(not_2_out), .out(multiplexer_2_out), .sel(Cin));
  Somador_Completo somador_completo_2 (
    .B(multiplexer_2_out), .Cout(somador_completo_2_cout), .Cin(somador_completo_3_cout), .S(S[6]), .A(A[6]));
  not not_3 (not_3_out, B[5]);
  Multiplexer #(.enable("false")) multiplexer_3 (.in0(B[5]), .in1(not_3_out), .out(multiplexer_3_out), .sel(Cin));
  Somador_Completo somador_completo_3 (
    .B(multiplexer_3_out), .Cout(somador_completo_3_cout), .Cin(somador_completo_4_cout), .S(S[5]), .A(A[5]));
  not not_4 (not_4_out, B[4]);
  Multiplexer #(.enable("false")) multiplexer_4 (.in0(B[4]), .in1(not_4_out), .out(multiplexer_4_out), .sel(Cin));
  Somador_Completo somador_completo_4 (
    .B(multiplexer_4_out), .Cout(somador_completo_4_cout), .Cin(somador_completo_5_cout), .S(S[4]), .A(A[4]));
  not not_5 (not_5_out, B[3]);
  Multiplexer #(.enable("false")) multiplexer_5 (.in0(B[3]), .in1(not_5_out), .out(multiplexer_5_out), .sel(Cin));
  Somador_Completo somador_completo_5 (
    .B(multiplexer_5_out), .Cout(somador_completo_5_cout), .Cin(somador_completo_6_cout), .S(S[3]), .A(A[3]));
  not not_6 (not_6_out, B[2]);
  Multiplexer #(.enable("false")) multiplexer_6 (.in0(B[2]), .in1(not_6_out), .out(multiplexer_6_out), .sel(Cin));
  Somador_Completo somador_completo_6 (
    .B(multiplexer_6_out), .Cout(somador_completo_6_cout), .Cin(somador_completo_7_cout), .S(S[2]), .A(A[2]));
  not not_7 (not_7_out, B[1]);
  Multiplexer #(.enable("false")) multiplexer_7 (.in0(B[1]), .in1(not_7_out), .out(multiplexer_7_out), .sel(Cin));
  Somador_Completo somador_completo_7 (
    .B(multiplexer_7_out), .Cout(somador_completo_7_cout), .Cin(somador_completo_8_cout), .S(S[1]), .A(A[1]));
  not not_8 (not_8_out, B[0]);
  Multiplexer #(.enable("false")) multiplexer_8 (.in0(B[0]), .in1(not_8_out), .out(multiplexer_8_out), .sel(Cin));
  Somador_Completo somador_completo_8 (
    .B(multiplexer_8_out), .Cout(somador_completo_8_cout), .Cin(Cin), .S(S[0]), .A(A[0]));
endmodule
