// Logisim project CAMINHO_DE_DADOS_C208A_03_11.circ as structural Verilog: 1 circuit, main circuit main
module main (
  input  MEM_TO_REG,
  input  [3:0] ALU_OP,
  input  ALU_SRC,
  input  MEM_W,
  input  REG_W,
  input  REG_DEST,
  input  MEM_R,
  input  RESET,
  output [4:0] out_9,
  output [4:0] out_10,
  output [4:0] out_11
);

  wire CLK, registerfile_1_p7;
  wire [31:0] adder_1_out, bit_extender_1_out, mips_alu_1_p4, mips_ram_1_p7, mipsprogramrom_1_p2,
       multiplexer_2_out, register_1_q, registerfile_1_p1, registerfile_1_p8;

  Clock clock_1 (.out(CLK));
  Adder #(.width(32)) adder_1 (.a(register_1_q), .b(32'h4), .out(adder_1_out));  // open: cin, cout
  Register #(.width(32)) register_1 (.D(adder_1_out), .Q(register_1_q), .clk(CLK));  // open: en, clr
  // MIPSProgramROM mipsprogramrom_1: pin names not known; wires that end beside it: register_1_q, {mipsprogramrom_1_p2[31:26], out_10, out_11, mipsprogramrom_1_p2[15:0]}
  Multiplexer #(.width(5)) multiplexer_1 (
    .in0(out_11), .in1(mipsprogramrom_1_p2[15:11]), .out(out_9), .sel(REG_DEST));  // open: en
  assign bit_extender_1_out = {{16{1'b0}}, mipsprogramrom_1_p2[15:0]};  // Bit_Extender bit_extender_1
  // RegisterFile registerfile_1: pin names not known; wires that end beside it: registerfile_1_p1, CLK, REG_W, out_9, out_10, out_11, registerfile_1_p7, registerfile_1_p8
  Multiplexer #(.width(32)) multiplexer_2 (
    .in0(registerfile_1_p8), .in1(bit_extender_1_out), .out(multiplexer_2_out), .sel(ALU_SRC));  // open: en
  // Mips_ALU mips_alu_1: pin names not known; wires that end beside it: registerfile_1_p7, multiplexer_2_out, ALU_OP, mips_alu_1_p4
  // MIPS_RAM mips_ram_1: pin names not known; wires that end beside it: mips_alu_1_p4[19:0], bit_extender_1_out, MEM_W, CLK, MEM_R, RESET, mips_ram_1_p7
  Multiplexer #(.width(32)) multiplexer_3 (
    .in0(mips_alu_1_p4), .in1(mips_ram_1_p7), .out(registerfile_1_p1), .sel(MEM_TO_REG));  // open: en

  // Notes on the sheet:
  //   CICLO DE BUSCA DA INSTRUÇÃO
  //   TIPO I
  //   TIPO R
  //   DADO A SER ESCRITO
  //   END. A SER ESCRITO
  //   LINHA DE WRITE BACK
endmodule
