// Logisim project CAMINHO_FINAL_2021_02.circ as structural Verilog: 1 circuit, main circuit main
module main (
  input  [3:0] in_1,
  output [5:0] out_2
);

  wire ALU_SRC, CLK, I_out, MEM_R, MEM_W, REG_DEST, REG_W, registerfile_1_p7, RESET;
  wire [4:0] multiplexer_1_out;
  wire [25:0] mipsprogramrom_1_p2;
  wire [31:0] adder_1_out, bit_extender_1_out, mips_alu_1_p4, mips_ram_1_p7, multiplexer_2_out, register_1_q,
       registerfile_1_p1, registerfile_1_p8;

  and R (REG_DEST, ~out_2[5], ~out_2[4], ~out_2[3], ~out_2[2], ~out_2[1], ~out_2[0]);  // AND_Gate
  and LW (MEM_R, out_2[5], ~out_2[4], ~out_2[3], ~out_2[2], out_2[1], out_2[0]);  // AND_Gate
  and SW (MEM_W, out_2[5], ~out_2[4], out_2[3], ~out_2[2], out_2[1], out_2[0]);  // AND_Gate
  Register #(.width(32)) register_1 (.D(adder_1_out), .Q(register_1_q), .clk(CLK));  // open: en, clr
  Adder #(.width(32)) adder_1 (.a(register_1_q), .b(32'h4), .out(adder_1_out));  // open: cin, cout
  and I (I_out, ~out_2[5], ~out_2[4], out_2[3], ~out_2[2], ~out_2[1], out_2[0]);  // AND_Gate
  Clock clock_1 (.out(CLK));
  or or_1 (ALU_SRC, MEM_W, I_out, MEM_R);
  or or_2 (REG_W, MEM_R, I_out, REG_DEST);
  // MIPSProgramROM mipsprogramrom_1: pin names not known; wires that end beside it: register_1_q, {out_2, mipsprogramrom_1_p2}
  Multiplexer #(.width(5), .enable("false")) multiplexer_1 (
    .in0(mipsprogramrom_1_p2[20:16]), .in1(mipsprogramrom_1_p2[15:11]), .out(multiplexer_1_out),
    .sel(REG_DEST));
  // RegisterFile registerfile_1: pin names not known; wires that end beside it: registerfile_1_p1, CLK, REG_W, multiplexer_1_out, mipsprogramrom_1_p2[25:21], mipsprogramrom_1_p2[20:16], registerfile_1_p7, registerfile_1_p8
  assign bit_extender_1_out = {{16{1'b0}}, mipsprogramrom_1_p2[15:0]};  // Bit_Extender bit_extender_1
  Multiplexer #(.width(32), .enable("false")) multiplexer_2 (
    .in0(registerfile_1_p8), .in1(bit_extender_1_out), .out(multiplexer_2_out), .sel(ALU_SRC));
  // Mips_ALU mips_alu_1: pin names not known; wires that end beside it: registerfile_1_p7, multiplexer_2_out, in_1, mips_alu_1_p4
  // MIPS_RAM mips_ram_1: pin names not known; wires that end beside it: mips_alu_1_p4[19:0], registerfile_1_p8, MEM_W, CLK, MEM_R, RESET, mips_ram_1_p7
  Multiplexer #(.width(32), .enable("false")) multiplexer_3 (
    .in0(mips_alu_1_p4), .in1(mips_ram_1_p7), .out(registerfile_1_p1), .sel(MEM_R));

  // Other names for the same wires on the sheet: OPCODE[5:0] = out_2; ALU_OP[3:0] = in_1; MEM_TO_REG = MEM_R

  // Notes on the sheet:
  //   CONTADOR DE PROGRAMA
  //   MEMÓRIA DE PROGRAMA
  //   TIPO I
  //   TIPO R
  //   WRITEBACK
endmodule
